# Fritzing sketch 4864P-tester (saved by Fritzing 0.9.3b)
breadboards: 1

parts:
  Part1 = Arduino Uno (Rev3)
  IC1 = IC, DIP package, 16 pins [chip_label=HM4864P-2]
  LED1 = LED - 5mm [color="Red (633nm)" package="5 mm [THT]"]
  Part2 = Breadboard Power Supply Board SMD

nets:
  N1: Part1.D8, IC1.pin4
  N2: Part1.D10_PWM/SS, IC1.pin3
  N3: Part1.D12/MISO, IC1.pin2
  N4: Part1.D13/SCK, LED1.anode
  GND: Part1.GND, LED1.cathode, Part2.GND
  VIN: Part1.VIN, Part2.VCC
